# Fritzing sketch diagram (saved by Fritzing 0.9.3b)
breadboards: 1

parts:
  Power_plug2 = Power plug  # not connected
  Raspberry_Pi_2 = Raspberry Pi 3 [part_number=RPI-3-V1.2]
  S1 = Square Pushbutton
  S2 = Square Pushbutton
  S3 = Square Pushbutton
  S4 = Square Pushbutton
  S5 = Square Pushbutton
  S6 = Square Pushbutton
  S7 = Square Pushbutton
  S8 = Square Pushbutton
  S9 = Square Pushbutton
  S10 = Square Pushbutton

nets:
  N1: Raspberry_Pi_2.GPIO2, S7.leg0
  N2: Raspberry_Pi_2.GPIO3, S3.leg0
  N3: Raspberry_Pi_2.GIPO4, S1.leg0
  N4: Raspberry_Pi_2.GND, S1.leg1, S2.leg1, S3.leg1, S4.leg1, S5.leg1, S6.leg1, S7.leg1, S8.leg1, S9.leg1, S10.leg1
  N5: Raspberry_Pi_2.GIPO7, S9.leg0
  N6: Raspberry_Pi_2.GIPO8, S8.leg0
  N7: Raspberry_Pi_2.GIPO25, S10.leg0
  N8: Raspberry_Pi_2.GIPO23, S4.leg0
  N9: Raspberry_Pi_2.GIPO18, S5.leg0
  N10: Raspberry_Pi_2.GIPO15, S6.leg0
  N11: Raspberry_Pi_2.GIPO14, S2.leg0

notes:
  5V power supply
